# Fritzing sketch Untitled Sketch2 (saved by Fritzing 0.9.7b)
breadboards: 1

parts:
  Part1 = Arduino Uno (Rev3) - ICSP
  L298N1 = L298N DC motor driver
  J1 = female pin header, 4 pins [form="♀ (female)"]

nets:
  N1: Part1.D8, L298N1.IN1
  N2: Part1.D9_PWM, L298N1.IN2
  N3: Part1.D10_PWM/SS, L298N1.IN3
  N4: Part1.D11_PWM/MOSI, L298N1.ENB, L298N1.IN4
  5V: Part1.5V, L298N1.5V
  GND: Part1.GND, L298N1.GND
  N5: L298N1.OUT1, J1.pin3
  N6: L298N1.OUT2, J1.pin4
  N7: L298N1.OUT3, J1.pin1
  N8: L298N1.OUT4, J1.pin2

custom parts:
  L298N DC motor driver: 2x DC motor driver with 78M05 positive voltage regulator (7..35 V) L298N: max 46 V, 2 A Set 5 V Enable jumper to enable 5 V regultor (needed for the L298N) and +5 V output at screw terminal or supply external +5 V at screw terminal Set ENA and/or ENB to +5 V to enable motor permanently or supply ENA and/or ENB with PWM signal IN1 and IN2 set rotation directory for motor A (OUT1/OUT2) IN2 and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
